# Fritzing sketch wiring (saved by Fritzing 0.9.9b)

parts:
  Inverter = Hex Inverter Schmitt Trigger SN74HC14 [package="DIP (Dual Inline)"]
  Knob_pins = Camdenboss CTB0158-4 [part_number=4=off package=THT]
  U1 = ESP 32 DEVKIT DOIT
  Knob_pins1 = Camdenboss CTB0158-3 [part_number=CTB0158-3 package=THT]
  Knob_pins2 = Camdenboss CTB0158-8 [part_number=CTB0158-8 package=THT]
  J1 = Camdenboss CTB0158-2 [part_number=CTB0158-2 package=THT]

nets (from the breadboard view):
  N1: Inverter.1A, U1.D13
  N2: Inverter.1Y, Knob_pins2.terminal_4
  N3: Inverter.2A, U1.D5, U1.D0, U1.SD1
  N4: Inverter.2Y, Knob_pins2.terminal_5
  N5: Inverter.3A, U1.D14
  N6: Inverter.3Y, Knob_pins2.terminal_6
  GND: Inverter.GND, Inverter.4A, Inverter.5A, U1.GND, Knob_pins1.terminal_2, J1.terminal_2
  N7: Inverter.6Y, Knob_pins2.terminal_7
  N8: Inverter.6A, U1.D27
  VCC: Inverter.VCC, U1.VIN, Knob_pins1.terminal_1
  N9: Knob_pins.terminal_1, U1.D25
  N10: Knob_pins.terminal_2, U1.D33
  N11: Knob_pins.terminal_3, U1.D32
  N12: Knob_pins.terminal_4, U1.D26
  N13: Knob_pins1.terminal_3, J1.terminal_1

notes:
  DC/DC-Coverter
  VIN
  VOUT
  GND
  KNOB
  1
  2
  3
  0
  FAN CONTROL CPU
  24V
  Board Voltage
